// Logisim project lab4(1).circ as structural Verilog: 1 circuit, main circuit main
module main (
  input  [7:0] in_1,
  input  [7:0] in_2,
  output [7:0] out_3,
  output [7:0] out_4,
  output [7:0] out_5,
  output [7:0] out_6
);

  wire and_1_out, and_2_out, and_3_out, and_4_out, and_5_out, and_6_out, and_7_out, and_8_out, and_9_out,
       and_10_out, and_11_out, and_12_out, and_13_out, and_14_out, and_15_out, and_16_out, C1, C2, C3, C4,
       C5, C6, C7, C8, not_1_out, not_2_out, not_3_out, not_4_out, not_5_out, not_6_out, not_7_out,
       not_8_out, not_9_out, not_10_out, not_11_out, not_12_out, not_13_out, not_14_out, not_15_out,
       not_16_out, xor_1_out, xor_2_out, xor_3_out, xor_4_out, xor_9_out, xor_10_out, xor_11_out, xor_12_out;

  LED led_1 (.in(C8));
  xor xor_1 (xor_1_out, in_1[0], in_2[0]);
  not not_1 (not_1_out, in_1[0]);
  xor xor_2 (xor_2_out, in_1[1], in_2[1]);
  not not_2 (not_2_out, in_1[1]);
  xor xor_3 (xor_3_out, in_1[2], in_2[2]);
  not not_3 (not_3_out, in_1[2]);
  xor xor_4 (xor_4_out, in_1[3], in_2[3]);
  not not_4 (not_4_out, in_1[3]);
  and and_1 (and_1_out, not_1_out, in_2[0]);
  and and_2 (and_2_out, not_2_out, in_2[1]);
  and and_3 (and_3_out, not_3_out, in_2[2]);
  and and_4 (and_4_out, not_4_out, in_2[3]);
  not not_5 (not_5_out, xor_1_out);
  not not_6 (not_6_out, xor_2_out);
  not not_7 (not_7_out, xor_3_out);
  not not_8 (not_8_out, xor_4_out);
  and and_5 (and_5_out, 1'b0, not_5_out);
  and and_6 (and_6_out, C1, not_6_out);
  and and_7 (and_7_out, C2, not_7_out);
  and and_8 (and_8_out, C3, not_8_out);
  xor xor_5 (out_5[0], xor_1_out, 1'b0);
  or or_1 (C1, and_5_out, and_1_out);
  xor xor_6 (out_5[1], xor_2_out, C1);
  or or_2 (C2, and_6_out, and_2_out);
  xor xor_7 (out_5[2], xor_3_out, C2);
  or or_3 (C3, and_7_out, and_3_out);
  xor xor_8 (out_5[3], xor_4_out, C3);
  or or_4 (C4, and_8_out, and_4_out);
  xor xor_9 (xor_9_out, in_1[4], in_2[4]);
  not not_9 (not_9_out, in_1[4]);
  xor xor_10 (xor_10_out, in_1[5], in_2[5]);
  not not_10 (not_10_out, in_1[5]);
  xor xor_11 (xor_11_out, in_1[6], in_2[6]);
  not not_11 (not_11_out, in_1[6]);
  xor xor_12 (xor_12_out, in_1[7], in_2[7]);
  not not_12 (not_12_out, in_1[7]);
  and and_9 (and_9_out, not_9_out, in_2[4]);
  and and_10 (and_10_out, not_10_out, in_2[5]);
  and and_11 (and_11_out, not_11_out, in_2[6]);
  and and_12 (and_12_out, not_12_out, in_2[7]);
  not not_13 (not_13_out, xor_9_out);
  not not_14 (not_14_out, xor_10_out);
  not not_15 (not_15_out, xor_11_out);
  not not_16 (not_16_out, xor_12_out);
  and and_13 (and_13_out, C4, not_13_out);
  and and_14 (and_14_out, C5, not_14_out);
  and and_15 (and_15_out, C6, not_15_out);
  and and_16 (and_16_out, C7, not_16_out);
  xor xor_13 (out_5[4], xor_9_out, C4);
  or or_5 (C5, and_13_out, and_9_out);
  xor xor_14 (out_5[5], xor_10_out, C5);
  or or_6 (C6, and_14_out, and_10_out);
  xor xor_15 (out_5[6], xor_11_out, C6);
  or or_7 (C7, and_15_out, and_11_out);
  xor xor_16 (out_5[7], xor_12_out, C7);
  or or_8 (C8, and_16_out, and_12_out);

  assign out_3 = in_1;
  assign out_4 = in_2;
  assign out_6 = out_5;

  // Other names for the same wires on the sheet: A0 = in_1[0]; A1 = in_1[1]; A2 = in_1[2]; A3 = in_1[3]; A4 = in_1[4];
  //   A5 = in_1[5]; A6 = in_1[6]; A7 = in_1[7]; B0 = in_2[0]; B1 = in_2[1]; B2 = in_2[2]; B3 = in_2[3]; B4 = in_2[4];
  //   B5 = in_2[5]; B6 = in_2[6]; B7 = in_2[7]; D0 = out_5[0]; D1 = out_5[1]; D2 = out_5[2]; D3 = out_5[3];
  //   D4 = out_5[4]; D5 = out_5[5]; D6 = out_5[6]; D7 = out_5[7]
endmodule
