// Logisim project CA.circ as structural Verilog: 1 circuit, main circuit main
module main (
  input  in_1,
  output out_2,
  output [2:0] out_3,
  output out_4,
  output out_5
);

  wire and_1_out, and_2_out, clock_1_out;

  and and_1 (and_1_out, in_1, out_3[0]);
  Clock clock_1 (.out(clock_1_out));
  and and_2 (and_2_out, out_3[1], and_1_out);
  T_Flip_Flop t_ff_1 (.T(and_2_out), .clk(clock_1_out), .Q(out_2));  // open: Qn, reset, preset
  T_Flip_Flop t_ff_2 (.T(and_1_out), .clk(clock_1_out), .Q(out_3[1]));  // open: Qn, reset, preset
  T_Flip_Flop t_ff_3 (.T(in_1), .clk(clock_1_out), .Q(out_3[0]));  // open: Qn, reset, preset

  assign out_3[2] = out_2;
  assign out_4 = out_3[1];
  assign out_5 = out_3[0];
endmodule
