// Logisim project 8_demultiplexer.circ as structural Verilog: 1 circuit, main circuit main
module main (
  input  D,
  input  S0,
  input  S1,
  input  S2,
  output Y0,
  output Y1,
  output Y2,
  output Y3,
  output Y4,
  output Y5,
  output Y6,
  output Y7
);

  wire not_1_out, not_2_out, not_3_out;

  not not_1 (not_1_out, S0);
  not not_2 (not_2_out, S1);
  not not_3 (not_3_out, S2);
  and and_1 (Y0, D, not_1_out, not_2_out, not_3_out);
  and and_2 (Y1, D, not_1_out, not_2_out, S2);
  and and_3 (Y2, D, not_1_out, S1, not_3_out);
  and and_4 (Y3, D, not_1_out, S1, S2);
  and and_5 (Y4, D, S0, not_2_out, not_3_out);
  and and_6 (Y5, D, S0, not_2_out, S2);
  and and_7 (Y6, D, S0, S1, not_3_out);
  and and_8 (Y7, S2, S1, S0, D);
endmodule
